# Fritzing sketch pong-oled (saved by Fritzing 0.9.10b)
breadboards: 1

parts:
  S1 = Pushbutton [package="[THT]"]
  Part1 = Arduino Uno (Rev3)
  OLED1 = 128x64 Monochrom OLED Display with SPI Control
  R1 = Rotary Potentiometer (Small) [maximum_resistance=100kΩ knob_status=50% power=0.5W package=THT]
  R2 = Rotary Potentiometer (Small) [maximum_resistance=100kΩ knob_status=50% power=0.5W package=THT]
  buz1 = Piezo Buzzer

nets:
  N1: S1.Pin_1, S1.Pin_2, Part1.D5_PWM
  GND: S1.Pin_3, S1.Pin_4, Part1.GND, OLED1.GND, R1.leg2, R2.leg2, buz1.pin_2
  N2: Part1.A1, R1.wiper
  N3: Part1.A2, R2.wiper
  N4: Part1.D8, buz1.pin_1
  N5: Part1.D9_PWM, OLED1.Data
  N6: Part1.D10_PWM/SS, OLED1.Clock
  N7: Part1.D11_PWM/MOSI, OLED1.SA0/DC
  N8: Part1.D12/MISO, OLED1.CS
  N9: Part1.D13/SCK, OLED1.Reset
  5V: Part1.5V, OLED1.Vin, R1.leg1, R2.leg1

custom parts:
  Piezo Buzzer: Part from https://www.nutsvolts.com/magazine/article/november2012_SmileysWorkshop. Breadboard and icon images modified to be 0.3" in spacing and be more similar to the actual physical part.
