# Fritzing sketch pong-tvout (saved by Fritzing 0.9.10b)
breadboards: 1

parts:
  S1 = Pushbutton [package="[THT]"]
  Part1 = Arduino Uno (Rev3)
  R1 = Rotary Potentiometer (Small) [maximum_resistance=100kΩ knob_status=50% power=0.5W package=THT]
  R2 = Rotary Potentiometer (Small) [maximum_resistance=100kΩ knob_status=50% power=0.5W package=THT]
  R3 = Resistor [tolerance=±5% power=0.25 resistance=1k package=THT]
  R4 = Resistor [tolerance=±5% power=0.25 resistance=470 package=THT]
  JP1 = RCA [package=rca_lock]

nets:
  N1: S1.Pin_1, S1.Pin_2, Part1.D5_PWM
  N2: S1.Pin_3, S1.Pin_4, Part1.GND, R1.leg2, R2.leg2, JP1.SWITCH
  N3: Part1.A1, R1.wiper
  N4: Part1.A2, R2.wiper
  N5: Part1.D9_PWM, R3.Pin_0
  N6: Part1.D7, R4.Pin_0
  N7: Part1.5V, R1.leg1, R2.leg1
  N8: R3.Pin_1, R4.Pin_1, JP1.PIN
